// Logisim project cpu.circ as structural Verilog: 10 circuits, main circuit main
module main (
  input  reset
);

  wire alu_1_lt, alu_1_ne, and_1_out, and_2_out, blt, bne, clk, iorR, j, jal, jr, keyboard_1_avail, le, lw,
       or_1_out, rkb, rwe, se, ttwe, wr7, wrt;
  wire [2:0] aluop, multiplexer_1_out, multiplexer_2_out;
  wire [3:0] opcode;
  wire [7:0] kbv;
  wire [11:0] address, PC;
  wire [15:0] alu_1_out, bigadder_1_result, bigadder_3_result, multiplexer_3_out, multiplexer_4_out,
       multiplexer_5_out, multiplexer_6_out, multiplexer_7_out, multiplexer_8_out, multiplexer_9_out, pc1,
       ram_1_data, rsv, swd, sxi;
  wire [15:12] L;

  Clock clock_1 (.out(clk));
  register register_1 (.clk(clk), .res(reset), .\input (multiplexer_7_out), .\output ({L, PC}));  // open: we
  bigadder bigadder_1 (.result(bigadder_1_result), .sub(1'b0), .B(16'h1), .A({L, PC}));  // open: ovf
  signextend signextend_1 (.\input (address[5:0]), .out(sxi));
  bigadder bigadder_2 (.result(pc1), .sub(1'b0), .B(16'h1), .A({L, PC}));  // open: ovf
  ROM #(.addrWidth(16), .dataWidth(16)) rom_1 (.addr({L, PC}), .data({opcode, address}));  // open: sel
  bigadder bigadder_3 (.result(bigadder_3_result), .sub(1'b0), .B(sxi), .A(bigadder_1_result));  // open: ovf
  RegisterFile registerfile_1 (
    .clk(clk), .reset(reset), .WriteData(multiplexer_9_out), .RegWE(rwe), .ReadR1(address[11:9]),
    .WriteReg(multiplexer_1_out), .ReadR2(address[8:6]), .r1(rsv), .r2(swd));
  Multiplexer #(.width(3), .enable("false")) multiplexer_1 (
    .in0(multiplexer_2_out), .in1(3'b111), .out(multiplexer_1_out), .sel(wr7));
  Multiplexer #(.width(3), .enable("false")) multiplexer_2 (
    .in0(address[5:3]), .in1(address[8:6]), .out(multiplexer_2_out), .sel(wrt));
  Keyboard keyboard_1 (.clk(clk), .clr(reset), .avail(keyboard_1_avail), .data(kbv[6:0]));  // open: re
  TTY #(.rows(13), .cols(80), .trigger("falling")) tty_1 (.data(rsv[6:0]), .clk(clk), .we(ttwe), .clr(reset));
  Multiplexer #(.width(16), .enable("false")) multiplexer_3 (.in0(swd), .in1(sxi), .out(multiplexer_3_out), .sel(iorR));
  not not_1 (kbv[7], keyboard_1_avail);
  alu alu_1 (
    .r1(rsv), .r2(multiplexer_3_out), .optype(aluop), .sham(address[2:0]), .lt(alu_1_lt), .ne(alu_1_ne),
    .out(alu_1_out));
  Multiplexer #(.width(16), .enable("false")) multiplexer_4 (
    .in0(bigadder_1_result), .in1(bigadder_3_result), .out(multiplexer_4_out), .sel(or_1_out));
  and and_1 (and_1_out, blt, alu_1_lt);
  and and_2 (and_2_out, bne, alu_1_ne);
  or or_1 (or_1_out, and_1_out, and_2_out);
  RAM #(.addrWidth(16), .dataWidth(16), .bus("separate")) ram_1 (
    .addr(alu_1_out), .din(swd), .data(ram_1_data), .str(se), .clk(clk), .ld(le));  // open: sel, clr
  Multiplexer #(.width(16), .enable("false")) multiplexer_5 (
    .in0(multiplexer_4_out), .in1({L, address}), .out(multiplexer_5_out), .sel(j));
  Multiplexer #(.width(16), .enable("false")) multiplexer_6 (
    .in0(alu_1_out), .in1(ram_1_data), .out(multiplexer_6_out), .sel(lw));
  Multiplexer #(.width(16), .enable("false")) multiplexer_7 (
    .in0(multiplexer_5_out), .in1(rsv), .out(multiplexer_7_out), .sel(jr));
  Multiplexer #(.width(16), .enable("false")) multiplexer_8 (
    .in0(multiplexer_6_out), .in1({{8{1'b0}}, kbv}), .out(multiplexer_8_out), .sel(rkb));
  Multiplexer #(.width(16), .enable("false")) multiplexer_9 (
    .in0(multiplexer_8_out), .in1(pc1), .out(multiplexer_9_out), .sel(jal));
  controlflow controlflow_1 (
    .opcode(opcode), .aluop(aluop), .rwe(rwe), .wrt(wrt), .wr7(wr7), .se(se), .le(le), .lw(lw), .rkb(rkb),
    .jal(jal), .ttwe(ttwe), .j(j), .blt(blt), .bne(bne), .jr(jr), .iorR(iorR));

  // Other names for the same wires on the sheet: imm[5:0] = address[5:0]; L[11:0] = address; sha[2:0] = address[2:0];
  //   struct[15:0] = {opcode, address}; rd[2:0] = address[5:3]; rt[2:0] = address[8:6]; rs[2:0] = address[11:9];
  //   PC[15:12] = L; res = reset
endmodule

module register (
  input  clk,
  input  we,
  input  res,
  input  [15:0] \input ,
  output [15:0] \output 
);

  D_Flip_Flop d_ff_1 (.clk(clk), .D(\input [0]), .Q(\output [0]), .en(we), .reset(res));  // open: Qn, preset
  D_Flip_Flop d_ff_2 (.clk(clk), .D(\input [2]), .Q(\output [2]), .en(we), .reset(res));  // open: Qn, preset
  D_Flip_Flop d_ff_3 (.clk(clk), .D(\input [4]), .Q(\output [4]), .en(we), .reset(res));  // open: Qn, preset
  D_Flip_Flop d_ff_4 (.clk(clk), .D(\input [6]), .Q(\output [6]), .en(we), .reset(res));  // open: Qn, preset
  D_Flip_Flop d_ff_5 (.clk(clk), .D(\input [8]), .Q(\output [8]), .en(we), .reset(res));  // open: Qn, preset
  D_Flip_Flop d_ff_6 (.clk(clk), .D(\input [10]), .Q(\output [10]), .en(we), .reset(res));  // open: Qn, preset
  D_Flip_Flop d_ff_7 (.clk(clk), .D(\input [12]), .Q(\output [12]), .en(we), .reset(res));  // open: Qn, preset
  D_Flip_Flop d_ff_8 (.clk(clk), .D(\input [14]), .Q(\output [14]), .en(we), .reset(res));  // open: Qn, preset
  D_Flip_Flop d_ff_9 (.clk(clk), .D(\input [1]), .Q(\output [1]), .en(we), .reset(res));  // open: Qn, preset
  D_Flip_Flop d_ff_10 (.clk(clk), .D(\input [3]), .Q(\output [3]), .en(we), .reset(res));  // open: Qn, preset
  D_Flip_Flop d_ff_11 (.clk(clk), .D(\input [5]), .Q(\output [5]), .en(we), .reset(res));  // open: Qn, preset
  D_Flip_Flop d_ff_12 (.clk(clk), .D(\input [7]), .Q(\output [7]), .en(we), .reset(res));  // open: Qn, preset
  D_Flip_Flop d_ff_13 (.clk(clk), .D(\input [9]), .Q(\output [9]), .en(we), .reset(res));  // open: Qn, preset
  D_Flip_Flop d_ff_14 (.clk(clk), .D(\input [11]), .Q(\output [11]), .en(we), .reset(res));  // open: Qn, preset
  D_Flip_Flop d_ff_15 (.clk(clk), .D(\input [13]), .Q(\output [13]), .en(we), .reset(res));  // open: Qn, preset
  D_Flip_Flop d_ff_16 (.clk(clk), .D(\input [15]), .Q(\output [15]), .en(we), .reset(res));  // open: Qn, preset
endmodule

module RegisterFile (
  input  clk,
  input  reset,
  input  [15:0] WriteData,
  input  RegWE,
  input  [2:0] ReadR1,
  input  [2:0] WriteReg,
  input  [2:0] ReadR2,
  output [15:0] r1,
  output [15:0] r2
);

  wire decoder_1_out1, decoder_1_out2, decoder_1_out3, decoder_1_out4, decoder_1_out5, decoder_1_out6,
       decoder_1_out7, r10, r11, r12, r13, r14, r15, r16, r17, r20, r21, r22, r23, r24, r25, r26, r27;
  wire [15:0] register_1_output, register_2_output, register_3_output, register_4_output, register_5_output,
       register_6_output, register_7_output, register_8_output;

  Decoder #(.select(3), .disabled(0)) decoder_1 (
    .out1(decoder_1_out1), .out2(decoder_1_out2), .out3(decoder_1_out3), .out4(decoder_1_out4),
    .out5(decoder_1_out5), .out6(decoder_1_out6), .out7(decoder_1_out7), .sel(WriteReg), .en(RegWE));  // open: out0
  register register_1 (.clk(clk), .we(1'b0), .res(reset), .\input (WriteData), .\output (register_1_output));
  register register_2 (.clk(clk), .we(decoder_1_out1), .res(reset), .\input (WriteData), .\output (register_2_output));
  register register_3 (.clk(clk), .we(decoder_1_out2), .res(reset), .\input (WriteData), .\output (register_3_output));
  register register_4 (.clk(clk), .we(decoder_1_out3), .res(reset), .\input (WriteData), .\output (register_4_output));
  register register_5 (.clk(clk), .we(decoder_1_out4), .res(reset), .\input (WriteData), .\output (register_5_output));
  register register_6 (.clk(clk), .we(decoder_1_out5), .res(reset), .\input (WriteData), .\output (register_6_output));
  register register_7 (.clk(clk), .we(decoder_1_out6), .res(reset), .\input (WriteData), .\output (register_7_output));
  register register_8 (.clk(clk), .we(decoder_1_out7), .res(reset), .\input (WriteData), .\output (register_8_output));
  // Probe on register_1_output
  assign r1 = r10 ? register_1_output : 16'bz;  // Controlled_Buffer controlled_buffer_1
  assign r1 = r11 ? register_2_output : 16'bz;  // Controlled_Buffer controlled_buffer_2
  assign r1 = r12 ? register_3_output : 16'bz;  // Controlled_Buffer controlled_buffer_3
  assign r1 = r13 ? register_4_output : 16'bz;  // Controlled_Buffer controlled_buffer_4
  assign r1 = r14 ? register_5_output : 16'bz;  // Controlled_Buffer controlled_buffer_5
  assign r1 = r15 ? register_6_output : 16'bz;  // Controlled_Buffer controlled_buffer_6
  assign r1 = r16 ? register_7_output : 16'bz;  // Controlled_Buffer controlled_buffer_7
  assign r1 = r17 ? register_8_output : 16'bz;  // Controlled_Buffer controlled_buffer_8
  // Probe on register_2_output
  // Probe on register_3_output
  // Probe on register_6_output
  // Probe on register_7_output
  // Probe on register_8_output
  assign r2 = r20 ? register_1_output : 16'bz;  // Controlled_Buffer controlled_buffer_9
  assign r2 = r21 ? register_2_output : 16'bz;  // Controlled_Buffer controlled_buffer_10
  assign r2 = r22 ? register_3_output : 16'bz;  // Controlled_Buffer controlled_buffer_11
  // Probe on register_4_output
  assign r2 = r23 ? register_4_output : 16'bz;  // Controlled_Buffer controlled_buffer_12
  assign r2 = r24 ? register_5_output : 16'bz;  // Controlled_Buffer controlled_buffer_13
  assign r2 = r25 ? register_6_output : 16'bz;  // Controlled_Buffer controlled_buffer_14
  assign r2 = r26 ? register_7_output : 16'bz;  // Controlled_Buffer controlled_buffer_15
  assign r2 = r27 ? register_8_output : 16'bz;  // Controlled_Buffer controlled_buffer_16
  // Probe on register_5_output
  Decoder #(.select(3), .enable("false")) decoder_2 (
    .out0(r10), .out1(r11), .out2(r12), .out3(r13), .out4(r14), .out5(r15), .out6(r16), .out7(r17),
    .sel(ReadR1));
  Decoder #(.select(3), .enable("false")) decoder_3 (
    .out0(r20), .out1(r21), .out2(r22), .out3(r23), .out4(r24), .out5(r25), .out6(r26), .out7(r27),
    .sel(ReadR2));

  // Other names for the same wires on the sheet: read1[15:0] = r1; read2[15:0] = r2; res = reset;
  //   wd[15:0] = WriteData
endmodule

module fulladder (
  input  Cin,
  input  A,
  input  B,
  output sum,
  output Cout
);

  wire and_1_out, and_2_out, xor_1_out;

  and and_1 (and_1_out, B, A);
  xor xor_1 (xor_1_out, A, B);
  or or_1 (Cout, and_1_out, and_2_out);
  and and_2 (and_2_out, xor_1_out, Cin);
  xor xor_2 (sum, Cin, xor_1_out);
endmodule

module bigadder (
  input  sub,
  input  [15:0] B,
  input  [15:0] A,
  output [15:0] result,
  output ovf
);

  wire fulladder_1_cout, fulladder_2_cout, fulladder_3_cout, fulladder_4_cout, fulladder_5_cout,
       fulladder_6_cout, fulladder_7_cout, fulladder_8_cout, fulladder_9_cout, fulladder_10_cout,
       fulladder_11_cout, fulladder_12_cout, fulladder_13_cout, fulladder_14_cout, fulladder_15_cout,
       fulladder_16_cout, xor_2_out, xor_3_out, xor_4_out, xor_5_out, xor_6_out, xor_7_out, xor_8_out,
       xor_9_out, xor_10_out, xor_11_out, xor_12_out, xor_13_out, xor_14_out, xor_15_out, xor_16_out,
       xor_17_out;

  xor xor_1 (ovf, fulladder_1_cout, fulladder_2_cout);
  fulladder fulladder_1 (.A(A[15]), .B(xor_2_out), .sum(result[15]), .Cin(fulladder_2_cout), .Cout(fulladder_1_cout));
  xor xor_2 (xor_2_out, sub, B[15]);
  fulladder fulladder_2 (.A(A[14]), .B(xor_3_out), .sum(result[14]), .Cin(fulladder_3_cout), .Cout(fulladder_2_cout));
  xor xor_3 (xor_3_out, sub, B[14]);
  fulladder fulladder_3 (.A(A[13]), .B(xor_4_out), .sum(result[13]), .Cin(fulladder_5_cout), .Cout(fulladder_3_cout));
  xor xor_4 (xor_4_out, sub, B[13]);
  fulladder fulladder_4 (.A(A[11]), .B(xor_6_out), .sum(result[11]), .Cin(fulladder_6_cout), .Cout(fulladder_4_cout));
  fulladder fulladder_5 (.A(A[12]), .B(xor_5_out), .sum(result[12]), .Cin(fulladder_4_cout), .Cout(fulladder_5_cout));
  xor xor_5 (xor_5_out, sub, B[12]);
  fulladder fulladder_6 (.A(A[10]), .B(xor_7_out), .sum(result[10]), .Cin(fulladder_7_cout), .Cout(fulladder_6_cout));
  xor xor_6 (xor_6_out, sub, B[11]);
  xor xor_7 (xor_7_out, sub, B[10]);
  fulladder fulladder_7 (.A(A[9]), .B(xor_8_out), .sum(result[9]), .Cin(fulladder_8_cout), .Cout(fulladder_7_cout));
  xor xor_8 (xor_8_out, sub, B[9]);
  fulladder fulladder_8 (.A(A[8]), .B(xor_9_out), .sum(result[8]), .Cin(fulladder_9_cout), .Cout(fulladder_8_cout));
  xor xor_9 (xor_9_out, sub, B[8]);
  fulladder fulladder_9 (.A(A[7]), .B(xor_10_out), .sum(result[7]), .Cin(fulladder_10_cout), .Cout(fulladder_9_cout));
  xor xor_10 (xor_10_out, sub, B[7]);
  fulladder fulladder_10 (.A(A[6]), .B(xor_11_out), .sum(result[6]), .Cin(fulladder_11_cout), .Cout(fulladder_10_cout));
  xor xor_11 (xor_11_out, sub, B[6]);
  fulladder fulladder_11 (.A(A[5]), .B(xor_12_out), .sum(result[5]), .Cin(fulladder_12_cout), .Cout(fulladder_11_cout));
  fulladder fulladder_12 (.A(A[4]), .B(xor_13_out), .sum(result[4]), .Cin(fulladder_13_cout), .Cout(fulladder_12_cout));
  xor xor_12 (xor_12_out, sub, B[5]);
  fulladder fulladder_13 (.A(A[3]), .B(xor_14_out), .sum(result[3]), .Cin(fulladder_14_cout), .Cout(fulladder_13_cout));
  xor xor_13 (xor_13_out, sub, B[4]);
  fulladder fulladder_14 (.A(A[2]), .B(xor_15_out), .sum(result[2]), .Cin(fulladder_15_cout), .Cout(fulladder_14_cout));
  xor xor_14 (xor_14_out, sub, B[3]);
  fulladder fulladder_15 (.A(A[1]), .B(xor_16_out), .sum(result[1]), .Cin(fulladder_16_cout), .Cout(fulladder_15_cout));
  xor xor_15 (xor_15_out, sub, B[2]);
  xor xor_16 (xor_16_out, sub, B[1]);
  fulladder fulladder_16 (.A(A[0]), .B(xor_17_out), .sum(result[0]), .Cin(sub), .Cout(fulladder_16_cout));
  xor xor_17 (xor_17_out, sub, B[0]);

  // Other names for the same wires on the sheet: aa = A[10]; ab = A[11]; ac = A[12]; ad = A[13]; ae = A[14];
  //   af = A[15]
endmodule

module leftshift (
  input  [15:0] shiftee,
  input  [15:0] shiftval,
  output [15:0] \output 
);

  wire c, multiplexer_1_out, multiplexer_2_out, multiplexer_3_out, multiplexer_4_out, multiplexer_5_out,
       multiplexer_6_out, multiplexer_7_out, multiplexer_8_out, multiplexer_9_out, multiplexer_10_out,
       multiplexer_11_out, multiplexer_12_out, multiplexer_13_out, multiplexer_14_out, multiplexer_15_out,
       multiplexer_16_out, multiplexer_17_out, multiplexer_18_out, multiplexer_19_out, multiplexer_20_out,
       multiplexer_21_out, multiplexer_22_out, multiplexer_23_out, multiplexer_24_out, multiplexer_25_out,
       multiplexer_26_out, multiplexer_27_out, multiplexer_28_out, multiplexer_29_out, multiplexer_30_out,
       multiplexer_31_out, multiplexer_32_out, multiplexer_33_out, multiplexer_34_out, multiplexer_35_out,
       multiplexer_36_out, multiplexer_37_out, multiplexer_38_out, multiplexer_39_out, multiplexer_40_out,
       multiplexer_41_out, multiplexer_42_out, multiplexer_43_out, multiplexer_44_out, multiplexer_45_out,
       multiplexer_46_out, multiplexer_47_out, multiplexer_48_out, not_1_out, r0, r1, r2, r3, r4, r5, r6, r7,
       r8, r9, r10, r11, r12, r13, r14, r15;

  or or_1 (c, shiftval[4], shiftval[5], shiftval[6], shiftval[7], shiftval[8], shiftval[9], shiftval[10], shiftval[11], shiftval[12], shiftval[13], shiftval[14], shiftval[15]);
  Multiplexer #(.enable("false")) multiplexer_1 (
    .in0(shiftee[15]), .in1(shiftee[7]), .out(multiplexer_1_out), .sel(shiftval[3]));
  Multiplexer #(.enable("false")) multiplexer_2 (
    .in0(shiftee[14]), .in1(shiftee[6]), .out(multiplexer_2_out), .sel(shiftval[3]));
  Multiplexer #(.enable("false")) multiplexer_3 (
    .in0(shiftee[13]), .in1(shiftee[5]), .out(multiplexer_3_out), .sel(shiftval[3]));
  Multiplexer #(.enable("false")) multiplexer_4 (
    .in0(shiftee[12]), .in1(shiftee[4]), .out(multiplexer_4_out), .sel(shiftval[3]));
  Multiplexer #(.enable("false")) multiplexer_5 (
    .in0(shiftee[11]), .in1(shiftee[3]), .out(multiplexer_5_out), .sel(shiftval[3]));
  Multiplexer #(.enable("false")) multiplexer_6 (
    .in0(shiftee[10]), .in1(shiftee[2]), .out(multiplexer_6_out), .sel(shiftval[3]));
  Multiplexer #(.enable("false")) multiplexer_7 (
    .in0(shiftee[9]), .in1(shiftee[1]), .out(multiplexer_7_out), .sel(shiftval[3]));
  Multiplexer #(.enable("false")) multiplexer_8 (
    .in0(shiftee[8]), .in1(shiftee[0]), .out(multiplexer_8_out), .sel(shiftval[3]));
  Multiplexer #(.enable("false")) multiplexer_9 (
    .in0(shiftee[7]), .in1(1'b0), .out(multiplexer_9_out), .sel(shiftval[3]));
  Multiplexer #(.enable("false")) multiplexer_10 (
    .in0(shiftee[6]), .in1(1'b0), .out(multiplexer_10_out), .sel(shiftval[3]));
  Multiplexer #(.enable("false")) multiplexer_11 (
    .in0(shiftee[5]), .in1(1'b0), .out(multiplexer_11_out), .sel(shiftval[3]));
  Multiplexer #(.enable("false")) multiplexer_12 (
    .in0(shiftee[4]), .in1(1'b0), .out(multiplexer_12_out), .sel(shiftval[3]));
  Multiplexer #(.enable("false")) multiplexer_13 (
    .in0(shiftee[3]), .in1(1'b0), .out(multiplexer_13_out), .sel(shiftval[3]));
  Multiplexer #(.enable("false")) multiplexer_14 (
    .in0(shiftee[2]), .in1(1'b0), .out(multiplexer_14_out), .sel(shiftval[3]));
  Multiplexer #(.enable("false")) multiplexer_15 (
    .in0(shiftee[1]), .in1(1'b0), .out(multiplexer_15_out), .sel(shiftval[3]));
  Multiplexer #(.enable("false")) multiplexer_16 (
    .in0(shiftee[0]), .in1(1'b0), .out(multiplexer_16_out), .sel(shiftval[3]));
  Multiplexer #(.enable("false")) multiplexer_17 (
    .in0(multiplexer_1_out), .in1(multiplexer_5_out), .out(multiplexer_17_out), .sel(shiftval[2]));
  Multiplexer #(.enable("false")) multiplexer_18 (
    .in0(multiplexer_2_out), .in1(multiplexer_6_out), .out(multiplexer_18_out), .sel(shiftval[2]));
  Multiplexer #(.enable("false")) multiplexer_19 (
    .in0(multiplexer_3_out), .in1(multiplexer_7_out), .out(multiplexer_19_out), .sel(shiftval[2]));
  Multiplexer #(.enable("false")) multiplexer_20 (
    .in0(multiplexer_4_out), .in1(multiplexer_8_out), .out(multiplexer_20_out), .sel(shiftval[2]));
  Multiplexer #(.enable("false")) multiplexer_21 (
    .in0(multiplexer_5_out), .in1(multiplexer_9_out), .out(multiplexer_21_out), .sel(shiftval[2]));
  Multiplexer #(.enable("false")) multiplexer_22 (
    .in0(multiplexer_6_out), .in1(multiplexer_10_out), .out(multiplexer_22_out), .sel(shiftval[2]));
  Multiplexer #(.enable("false")) multiplexer_23 (
    .in0(multiplexer_7_out), .in1(multiplexer_11_out), .out(multiplexer_23_out), .sel(shiftval[2]));
  Multiplexer #(.enable("false")) multiplexer_24 (
    .in0(multiplexer_8_out), .in1(multiplexer_12_out), .out(multiplexer_24_out), .sel(shiftval[2]));
  Multiplexer #(.enable("false")) multiplexer_25 (
    .in0(multiplexer_9_out), .in1(multiplexer_13_out), .out(multiplexer_25_out), .sel(shiftval[2]));
  Multiplexer #(.enable("false")) multiplexer_26 (
    .in0(multiplexer_10_out), .in1(multiplexer_14_out), .out(multiplexer_26_out), .sel(shiftval[2]));
  Multiplexer #(.enable("false")) multiplexer_27 (
    .in0(multiplexer_11_out), .in1(multiplexer_15_out), .out(multiplexer_27_out), .sel(shiftval[2]));
  Multiplexer #(.enable("false")) multiplexer_28 (
    .in0(multiplexer_12_out), .in1(multiplexer_16_out), .out(multiplexer_28_out), .sel(shiftval[2]));
  Multiplexer #(.enable("false")) multiplexer_29 (
    .in0(multiplexer_13_out), .in1(1'b0), .out(multiplexer_29_out), .sel(shiftval[2]));
  Multiplexer #(.enable("false")) multiplexer_30 (
    .in0(multiplexer_14_out), .in1(1'b0), .out(multiplexer_30_out), .sel(shiftval[2]));
  Multiplexer #(.enable("false")) multiplexer_31 (
    .in0(multiplexer_15_out), .in1(1'b0), .out(multiplexer_31_out), .sel(shiftval[2]));
  Multiplexer #(.enable("false")) multiplexer_32 (
    .in0(multiplexer_16_out), .in1(1'b0), .out(multiplexer_32_out), .sel(shiftval[2]));
  Multiplexer #(.enable("false")) multiplexer_33 (
    .in0(multiplexer_17_out), .in1(multiplexer_19_out), .out(multiplexer_33_out), .sel(shiftval[1]));
  Multiplexer #(.enable("false")) multiplexer_34 (
    .in0(multiplexer_18_out), .in1(multiplexer_20_out), .out(multiplexer_34_out), .sel(shiftval[1]));
  Multiplexer #(.enable("false")) multiplexer_35 (
    .in0(multiplexer_19_out), .in1(multiplexer_21_out), .out(multiplexer_35_out), .sel(shiftval[1]));
  Multiplexer #(.enable("false")) multiplexer_36 (
    .in0(multiplexer_20_out), .in1(multiplexer_22_out), .out(multiplexer_36_out), .sel(shiftval[1]));
  Multiplexer #(.enable("false")) multiplexer_37 (
    .in0(multiplexer_21_out), .in1(multiplexer_23_out), .out(multiplexer_37_out), .sel(shiftval[1]));
  Multiplexer #(.enable("false")) multiplexer_38 (
    .in0(multiplexer_22_out), .in1(multiplexer_24_out), .out(multiplexer_38_out), .sel(shiftval[1]));
  Multiplexer #(.enable("false")) multiplexer_39 (
    .in0(multiplexer_23_out), .in1(multiplexer_25_out), .out(multiplexer_39_out), .sel(shiftval[1]));
  Multiplexer #(.enable("false")) multiplexer_40 (
    .in0(multiplexer_24_out), .in1(multiplexer_26_out), .out(multiplexer_40_out), .sel(shiftval[1]));
  Multiplexer #(.enable("false")) multiplexer_41 (
    .in0(multiplexer_25_out), .in1(multiplexer_27_out), .out(multiplexer_41_out), .sel(shiftval[1]));
  Multiplexer #(.enable("false")) multiplexer_42 (
    .in0(multiplexer_26_out), .in1(multiplexer_28_out), .out(multiplexer_42_out), .sel(shiftval[1]));
  Multiplexer #(.enable("false")) multiplexer_43 (
    .in0(multiplexer_27_out), .in1(multiplexer_29_out), .out(multiplexer_43_out), .sel(shiftval[1]));
  Multiplexer #(.enable("false")) multiplexer_44 (
    .in0(multiplexer_28_out), .in1(multiplexer_30_out), .out(multiplexer_44_out), .sel(shiftval[1]));
  Multiplexer #(.enable("false")) multiplexer_45 (
    .in0(multiplexer_29_out), .in1(multiplexer_31_out), .out(multiplexer_45_out), .sel(shiftval[1]));
  Multiplexer #(.enable("false")) multiplexer_46 (
    .in0(multiplexer_30_out), .in1(multiplexer_32_out), .out(multiplexer_46_out), .sel(shiftval[1]));
  Multiplexer #(.enable("false")) multiplexer_47 (
    .in0(multiplexer_31_out), .in1(1'b0), .out(multiplexer_47_out), .sel(shiftval[1]));
  Multiplexer #(.enable("false")) multiplexer_48 (
    .in0(multiplexer_32_out), .in1(1'b0), .out(multiplexer_48_out), .sel(shiftval[1]));
  Multiplexer #(.enable("false")) multiplexer_49 (
    .in0(multiplexer_33_out), .in1(multiplexer_34_out), .out(r15), .sel(shiftval[0]));
  Multiplexer #(.enable("false")) multiplexer_50 (
    .in0(multiplexer_34_out), .in1(multiplexer_35_out), .out(r14), .sel(shiftval[0]));
  Multiplexer #(.enable("false")) multiplexer_51 (
    .in0(multiplexer_35_out), .in1(multiplexer_36_out), .out(r13), .sel(shiftval[0]));
  Multiplexer #(.enable("false")) multiplexer_52 (
    .in0(multiplexer_36_out), .in1(multiplexer_37_out), .out(r12), .sel(shiftval[0]));
  Multiplexer #(.enable("false")) multiplexer_53 (
    .in0(multiplexer_37_out), .in1(multiplexer_38_out), .out(r11), .sel(shiftval[0]));
  Multiplexer #(.enable("false")) multiplexer_54 (
    .in0(multiplexer_38_out), .in1(multiplexer_39_out), .out(r10), .sel(shiftval[0]));
  Multiplexer #(.enable("false")) multiplexer_55 (
    .in0(multiplexer_39_out), .in1(multiplexer_40_out), .out(r9), .sel(shiftval[0]));
  Multiplexer #(.enable("false")) multiplexer_56 (
    .in0(multiplexer_40_out), .in1(multiplexer_41_out), .out(r8), .sel(shiftval[0]));
  Multiplexer #(.enable("false")) multiplexer_57 (
    .in0(multiplexer_41_out), .in1(multiplexer_42_out), .out(r7), .sel(shiftval[0]));
  Multiplexer #(.enable("false")) multiplexer_58 (
    .in0(multiplexer_42_out), .in1(multiplexer_43_out), .out(r6), .sel(shiftval[0]));
  Multiplexer #(.enable("false")) multiplexer_59 (
    .in0(multiplexer_43_out), .in1(multiplexer_44_out), .out(r5), .sel(shiftval[0]));
  Multiplexer #(.enable("false")) multiplexer_60 (
    .in0(multiplexer_44_out), .in1(multiplexer_45_out), .out(r4), .sel(shiftval[0]));
  Multiplexer #(.enable("false")) multiplexer_61 (
    .in0(multiplexer_45_out), .in1(multiplexer_46_out), .out(r3), .sel(shiftval[0]));
  Multiplexer #(.enable("false")) multiplexer_62 (
    .in0(multiplexer_46_out), .in1(multiplexer_47_out), .out(r2), .sel(shiftval[0]));
  Multiplexer #(.enable("false")) multiplexer_63 (
    .in0(multiplexer_47_out), .in1(multiplexer_48_out), .out(r1), .sel(shiftval[0]));
  Multiplexer #(.enable("false")) multiplexer_64 (.in0(multiplexer_48_out), .in1(1'b0), .out(r0), .sel(shiftval[0]));
  assign \output  = not_1_out ? {r15, r14, r13, r12, r11, r10, r9, r8, r7, r6, r5, r4, r3, r2, r1, r0} : 16'bz;  // Controlled_Buffer controlled_buffer_1
  not not_1 (not_1_out, c);
  assign \output  = c ? {16{1'b0}} : 16'bz;  // Controlled_Buffer controlled_buffer_2

  // Other names for the same wires on the sheet: _0 = shiftee[0]; _1 = shiftee[1]; _2 = shiftee[2]; _3 = shiftee[3];
  //   _4 = shiftee[4]; _5 = shiftee[5]; _6 = shiftee[6]; _7 = shiftee[7]; _8 = shiftee[8]; _9 = shiftee[9];
  //   _10 = shiftee[10]; _11 = shiftee[11]; _12 = shiftee[12]; _13 = shiftee[13]; _14 = shiftee[14];
  //   _15 = shiftee[15]; s1 = shiftval[0]; s2 = shiftval[1]; s3 = shiftval[2]; s4 = shiftval[3]
endmodule

module rshift (
  input  [15:0] shiftee,
  input  [15:0] shiftval,
  output [15:0] \output 
);

  wire c, multiplexer_1_out, multiplexer_2_out, multiplexer_3_out, multiplexer_4_out, multiplexer_5_out,
       multiplexer_6_out, multiplexer_7_out, multiplexer_8_out, multiplexer_9_out, multiplexer_10_out,
       multiplexer_11_out, multiplexer_12_out, multiplexer_13_out, multiplexer_14_out, multiplexer_15_out,
       multiplexer_16_out, multiplexer_17_out, multiplexer_18_out, multiplexer_19_out, multiplexer_20_out,
       multiplexer_21_out, multiplexer_22_out, multiplexer_23_out, multiplexer_24_out, multiplexer_25_out,
       multiplexer_26_out, multiplexer_27_out, multiplexer_28_out, multiplexer_29_out, multiplexer_30_out,
       multiplexer_31_out, multiplexer_32_out, multiplexer_33_out, multiplexer_34_out, multiplexer_35_out,
       multiplexer_36_out, multiplexer_37_out, multiplexer_38_out, multiplexer_39_out, multiplexer_40_out,
       multiplexer_41_out, multiplexer_42_out, multiplexer_43_out, multiplexer_44_out, multiplexer_45_out,
       multiplexer_46_out, multiplexer_47_out, multiplexer_48_out, not_1_out, r0, r1, r2, r3, r4, r5, r6, r7,
       r8, r9, r10, r11, r12, r13, r14, r15;

  or or_1 (c, shiftval[4], shiftval[5], shiftval[6], shiftval[7], shiftval[8], shiftval[9], shiftval[10], shiftval[11], shiftval[12], shiftval[13], shiftval[14], shiftval[15]);
  Multiplexer #(.enable("false")) multiplexer_1 (
    .in0(shiftee[0]), .in1(shiftee[8]), .out(multiplexer_1_out), .sel(shiftval[3]));
  Multiplexer #(.enable("false")) multiplexer_2 (
    .in0(shiftee[1]), .in1(shiftee[9]), .out(multiplexer_2_out), .sel(shiftval[3]));
  Multiplexer #(.enable("false")) multiplexer_3 (
    .in0(shiftee[2]), .in1(shiftee[10]), .out(multiplexer_3_out), .sel(shiftval[3]));
  Multiplexer #(.enable("false")) multiplexer_4 (
    .in0(shiftee[3]), .in1(shiftee[11]), .out(multiplexer_4_out), .sel(shiftval[3]));
  Multiplexer #(.enable("false")) multiplexer_5 (
    .in0(shiftee[4]), .in1(shiftee[12]), .out(multiplexer_5_out), .sel(shiftval[3]));
  Multiplexer #(.enable("false")) multiplexer_6 (
    .in0(shiftee[5]), .in1(shiftee[13]), .out(multiplexer_6_out), .sel(shiftval[3]));
  Multiplexer #(.enable("false")) multiplexer_7 (
    .in0(shiftee[6]), .in1(shiftee[14]), .out(multiplexer_7_out), .sel(shiftval[3]));
  Multiplexer #(.enable("false")) multiplexer_8 (
    .in0(shiftee[7]), .in1(shiftee[15]), .out(multiplexer_8_out), .sel(shiftval[3]));
  Multiplexer #(.enable("false")) multiplexer_9 (
    .in0(shiftee[8]), .in1(1'b0), .out(multiplexer_9_out), .sel(shiftval[3]));
  Multiplexer #(.enable("false")) multiplexer_10 (
    .in0(shiftee[9]), .in1(1'b0), .out(multiplexer_10_out), .sel(shiftval[3]));
  Multiplexer #(.enable("false")) multiplexer_11 (
    .in0(shiftee[10]), .in1(1'b0), .out(multiplexer_11_out), .sel(shiftval[3]));
  Multiplexer #(.enable("false")) multiplexer_12 (
    .in0(shiftee[11]), .in1(1'b0), .out(multiplexer_12_out), .sel(shiftval[3]));
  Multiplexer #(.enable("false")) multiplexer_13 (
    .in0(shiftee[12]), .in1(1'b0), .out(multiplexer_13_out), .sel(shiftval[3]));
  Multiplexer #(.enable("false")) multiplexer_14 (
    .in0(shiftee[13]), .in1(1'b0), .out(multiplexer_14_out), .sel(shiftval[3]));
  Multiplexer #(.enable("false")) multiplexer_15 (
    .in0(shiftee[14]), .in1(1'b0), .out(multiplexer_15_out), .sel(shiftval[3]));
  Multiplexer #(.enable("false")) multiplexer_16 (
    .in0(shiftee[15]), .in1(1'b0), .out(multiplexer_16_out), .sel(shiftval[3]));
  Multiplexer #(.enable("false")) multiplexer_17 (
    .in0(multiplexer_1_out), .in1(multiplexer_5_out), .out(multiplexer_17_out), .sel(shiftval[2]));
  Multiplexer #(.enable("false")) multiplexer_18 (
    .in0(multiplexer_2_out), .in1(multiplexer_6_out), .out(multiplexer_18_out), .sel(shiftval[2]));
  Multiplexer #(.enable("false")) multiplexer_19 (
    .in0(multiplexer_3_out), .in1(multiplexer_7_out), .out(multiplexer_19_out), .sel(shiftval[2]));
  Multiplexer #(.enable("false")) multiplexer_20 (
    .in0(multiplexer_4_out), .in1(multiplexer_8_out), .out(multiplexer_20_out), .sel(shiftval[2]));
  Multiplexer #(.enable("false")) multiplexer_21 (
    .in0(multiplexer_5_out), .in1(multiplexer_9_out), .out(multiplexer_21_out), .sel(shiftval[2]));
  Multiplexer #(.enable("false")) multiplexer_22 (
    .in0(multiplexer_6_out), .in1(multiplexer_10_out), .out(multiplexer_22_out), .sel(shiftval[2]));
  Multiplexer #(.enable("false")) multiplexer_23 (
    .in0(multiplexer_7_out), .in1(multiplexer_11_out), .out(multiplexer_23_out), .sel(shiftval[2]));
  Multiplexer #(.enable("false")) multiplexer_24 (
    .in0(multiplexer_8_out), .in1(multiplexer_12_out), .out(multiplexer_24_out), .sel(shiftval[2]));
  Multiplexer #(.enable("false")) multiplexer_25 (
    .in0(multiplexer_9_out), .in1(multiplexer_13_out), .out(multiplexer_25_out), .sel(shiftval[2]));
  Multiplexer #(.enable("false")) multiplexer_26 (
    .in0(multiplexer_10_out), .in1(multiplexer_14_out), .out(multiplexer_26_out), .sel(shiftval[2]));
  Multiplexer #(.enable("false")) multiplexer_27 (
    .in0(multiplexer_11_out), .in1(multiplexer_15_out), .out(multiplexer_27_out), .sel(shiftval[2]));
  Multiplexer #(.enable("false")) multiplexer_28 (
    .in0(multiplexer_12_out), .in1(multiplexer_16_out), .out(multiplexer_28_out), .sel(shiftval[2]));
  Multiplexer #(.enable("false")) multiplexer_29 (
    .in0(multiplexer_13_out), .in1(1'b0), .out(multiplexer_29_out), .sel(shiftval[2]));
  Multiplexer #(.enable("false")) multiplexer_30 (
    .in0(multiplexer_14_out), .in1(1'b0), .out(multiplexer_30_out), .sel(shiftval[2]));
  Multiplexer #(.enable("false")) multiplexer_31 (
    .in0(multiplexer_15_out), .in1(1'b0), .out(multiplexer_31_out), .sel(shiftval[2]));
  Multiplexer #(.enable("false")) multiplexer_32 (
    .in0(multiplexer_16_out), .in1(1'b0), .out(multiplexer_32_out), .sel(shiftval[2]));
  Multiplexer #(.enable("false")) multiplexer_33 (
    .in0(multiplexer_17_out), .in1(multiplexer_19_out), .out(multiplexer_33_out), .sel(shiftval[1]));
  Multiplexer #(.enable("false")) multiplexer_34 (
    .in0(multiplexer_18_out), .in1(multiplexer_20_out), .out(multiplexer_34_out), .sel(shiftval[1]));
  Multiplexer #(.enable("false")) multiplexer_35 (
    .in0(multiplexer_19_out), .in1(multiplexer_21_out), .out(multiplexer_35_out), .sel(shiftval[1]));
  Multiplexer #(.enable("false")) multiplexer_36 (
    .in0(multiplexer_20_out), .in1(multiplexer_22_out), .out(multiplexer_36_out), .sel(shiftval[1]));
  Multiplexer #(.enable("false")) multiplexer_37 (
    .in0(multiplexer_21_out), .in1(multiplexer_23_out), .out(multiplexer_37_out), .sel(shiftval[1]));
  Multiplexer #(.enable("false")) multiplexer_38 (
    .in0(multiplexer_22_out), .in1(multiplexer_24_out), .out(multiplexer_38_out), .sel(shiftval[1]));
  Multiplexer #(.enable("false")) multiplexer_39 (
    .in0(multiplexer_23_out), .in1(multiplexer_25_out), .out(multiplexer_39_out), .sel(shiftval[1]));
  Multiplexer #(.enable("false")) multiplexer_40 (
    .in0(multiplexer_24_out), .in1(multiplexer_26_out), .out(multiplexer_40_out), .sel(shiftval[1]));
  Multiplexer #(.enable("false")) multiplexer_41 (
    .in0(multiplexer_25_out), .in1(multiplexer_27_out), .out(multiplexer_41_out), .sel(shiftval[1]));
  Multiplexer #(.enable("false")) multiplexer_42 (
    .in0(multiplexer_26_out), .in1(multiplexer_28_out), .out(multiplexer_42_out), .sel(shiftval[1]));
  Multiplexer #(.enable("false")) multiplexer_43 (
    .in0(multiplexer_27_out), .in1(multiplexer_29_out), .out(multiplexer_43_out), .sel(shiftval[1]));
  Multiplexer #(.enable("false")) multiplexer_44 (
    .in0(multiplexer_28_out), .in1(multiplexer_30_out), .out(multiplexer_44_out), .sel(shiftval[1]));
  Multiplexer #(.enable("false")) multiplexer_45 (
    .in0(multiplexer_29_out), .in1(multiplexer_31_out), .out(multiplexer_45_out), .sel(shiftval[1]));
  Multiplexer #(.enable("false")) multiplexer_46 (
    .in0(multiplexer_30_out), .in1(multiplexer_32_out), .out(multiplexer_46_out), .sel(shiftval[1]));
  Multiplexer #(.enable("false")) multiplexer_47 (
    .in0(multiplexer_31_out), .in1(1'b0), .out(multiplexer_47_out), .sel(shiftval[1]));
  Multiplexer #(.enable("false")) multiplexer_48 (
    .in0(multiplexer_32_out), .in1(1'b0), .out(multiplexer_48_out), .sel(shiftval[1]));
  Multiplexer #(.enable("false")) multiplexer_49 (
    .in0(multiplexer_33_out), .in1(multiplexer_34_out), .out(r0), .sel(shiftval[0]));
  Multiplexer #(.enable("false")) multiplexer_50 (
    .in0(multiplexer_34_out), .in1(multiplexer_35_out), .out(r1), .sel(shiftval[0]));
  Multiplexer #(.enable("false")) multiplexer_51 (
    .in0(multiplexer_35_out), .in1(multiplexer_36_out), .out(r2), .sel(shiftval[0]));
  Multiplexer #(.enable("false")) multiplexer_52 (
    .in0(multiplexer_36_out), .in1(multiplexer_37_out), .out(r3), .sel(shiftval[0]));
  Multiplexer #(.enable("false")) multiplexer_53 (
    .in0(multiplexer_37_out), .in1(multiplexer_38_out), .out(r4), .sel(shiftval[0]));
  Multiplexer #(.enable("false")) multiplexer_54 (
    .in0(multiplexer_38_out), .in1(multiplexer_39_out), .out(r5), .sel(shiftval[0]));
  Multiplexer #(.enable("false")) multiplexer_55 (
    .in0(multiplexer_39_out), .in1(multiplexer_40_out), .out(r6), .sel(shiftval[0]));
  Multiplexer #(.enable("false")) multiplexer_56 (
    .in0(multiplexer_40_out), .in1(multiplexer_41_out), .out(r7), .sel(shiftval[0]));
  Multiplexer #(.enable("false")) multiplexer_57 (
    .in0(multiplexer_41_out), .in1(multiplexer_42_out), .out(r8), .sel(shiftval[0]));
  Multiplexer #(.enable("false")) multiplexer_58 (
    .in0(multiplexer_42_out), .in1(multiplexer_43_out), .out(r9), .sel(shiftval[0]));
  Multiplexer #(.enable("false")) multiplexer_59 (
    .in0(multiplexer_43_out), .in1(multiplexer_44_out), .out(r10), .sel(shiftval[0]));
  Multiplexer #(.enable("false")) multiplexer_60 (
    .in0(multiplexer_44_out), .in1(multiplexer_45_out), .out(r11), .sel(shiftval[0]));
  Multiplexer #(.enable("false")) multiplexer_61 (
    .in0(multiplexer_45_out), .in1(multiplexer_46_out), .out(r12), .sel(shiftval[0]));
  Multiplexer #(.enable("false")) multiplexer_62 (
    .in0(multiplexer_46_out), .in1(multiplexer_47_out), .out(r13), .sel(shiftval[0]));
  Multiplexer #(.enable("false")) multiplexer_63 (
    .in0(multiplexer_47_out), .in1(multiplexer_48_out), .out(r14), .sel(shiftval[0]));
  Multiplexer #(.enable("false")) multiplexer_64 (.in0(multiplexer_48_out), .in1(1'b0), .out(r15), .sel(shiftval[0]));
  assign \output  = not_1_out ? {r15, r14, r13, r12, r11, r10, r9, r8, r7, r6, r5, r4, r3, r2, r1, r0} : 16'bz;  // Controlled_Buffer controlled_buffer_1
  not not_1 (not_1_out, c);
  assign \output  = c ? {16{1'b0}} : 16'bz;  // Controlled_Buffer controlled_buffer_2

  // Other names for the same wires on the sheet: _0 = shiftee[0]; _1 = shiftee[1]; _2 = shiftee[2]; _3 = shiftee[3];
  //   _4 = shiftee[4]; _5 = shiftee[5]; _6 = shiftee[6]; _7 = shiftee[7]; _8 = shiftee[8]; _9 = shiftee[9];
  //   _10 = shiftee[10]; _11 = shiftee[11]; _12 = shiftee[12]; _13 = shiftee[13]; _14 = shiftee[14];
  //   _15 = shiftee[15]; s1 = shiftval[0]; s2 = shiftval[1]; s3 = shiftval[2]; s4 = shiftval[3]
endmodule

module alu (
  input  [15:0] r1,
  input  [15:0] r2,
  input  [2:0] optype,
  input  [2:0] sham,
  output lt,
  output ne,
  output [15:0] out
);

  wire [15:0] bigadder_1_result, bigadder_2_result, bigadder_3_result, leftshift_1_output, not_1_out,
       rshift_1_output, xor_1_out;

  bigadder bigadder_1 (.result(bigadder_1_result), .sub(1'b0), .B(r2), .A(r1));  // open: ovf
  bigadder bigadder_2 (.result(bigadder_2_result), .sub(1'b0), .B(r2), .A(r1));  // open: ovf
  bigadder bigadder_3 (.result(bigadder_3_result), .sub(1'b1), .B(r2), .A(r1));  // open: ovf
  assign not_1_out = ~r1;  // NOT_Gate not_1, 16 bits wide
  leftshift leftshift_1 (.shiftee(r1), .shiftval({{13{1'b0}}, sham}), .\output (leftshift_1_output));
  rshift rshift_1 (.shiftee(r1), .shiftval({{13{1'b0}}, sham}), .\output (rshift_1_output));
  assign xor_1_out = r1 ^ r2;  // XOR_Gate xor_1, 16 bits wide
  Multiplexer #(.select(3), .width(16), .disabled(0)) multiplexer_1 (
    .in0(bigadder_1_result), .in1(bigadder_2_result), .in2(bigadder_3_result), .in3(not_1_out),
    .in4(xor_1_out), .in5(leftshift_1_output), .in6(rshift_1_output), .out({lt, out[14:0]}), .sel(optype),
    .en(1'b1));  // open: in7
  or or_1 (ne, out[0], out[1], out[2], out[3], out[4], out[5], out[6], out[7], out[8], out[9], out[10], out[11], out[12], out[13], out[14], lt);

  assign out[15] = lt;

  // Other names for the same wires on the sheet: op[2:0] = optype; ret[15:0] = {lt, out[14:0]}; sham_t[2:0] = sham
endmodule

module controlflow (
  input  [3:0] opcode,
  output rwe,
  output wrt,
  output wr7,
  output se,
  output le,
  output lw,
  output rkb,
  output jal,
  output ttwe,
  output j,
  output blt,
  output bne,
  output jr,
  output iorR,
  output [2:0] aluop
);

  wire add, addi, j_t, \not , or_1_out, or_2_out, or_3_out, sll, srl, sub, \xor ;

  Decoder #(.select(4), .enable("false")) decoder_1 (
    .out0(add), .out1(addi), .out2(sub), .out3(\not ), .out4(\xor ), .out5(sll), .out6(srl), .out7(le),
    .out8(se), .out9(bne), .out10(blt), .out11(j_t), .out12(jr), .out13(jal), .out14(rkb), .out15(ttwe),
    .sel(opcode));
  or or_1 (or_1_out, j_t, jr, rkb, jal, ttwe);
  assign aluop = or_2_out ? 3'b000 : 3'bz;  // Controlled_Buffer controlled_buffer_1
  or or_2 (or_2_out, add, addi, le, se);
  assign aluop = or_3_out ? 3'b010 : 3'bz;  // Controlled_Buffer controlled_buffer_2
  or or_3 (or_3_out, blt, bne, sub);
  assign aluop = \not  ? 3'b011 : 3'bz;  // Controlled_Buffer controlled_buffer_3
  assign aluop = \xor  ? 3'b100 : 3'bz;  // Controlled_Buffer controlled_buffer_4
  assign aluop = sll ? 3'b101 : 3'bz;  // Controlled_Buffer controlled_buffer_5
  assign aluop = srl ? 3'b110 : 3'bz;  // Controlled_Buffer controlled_buffer_6
  assign aluop = or_1_out ? 3'b000 : 3'bz;  // Controlled_Buffer controlled_buffer_7
  or or_4 (rwe, rkb, jal, le, srl, sll, \xor , \not , sub, addi, add);
  or or_5 (wrt, rkb, le, addi);
  or or_6 (j, jal, j_t);
  or or_7 (iorR, se, addi, le);

  assign lw = le;
  assign wr7 = jal;

  // Other names for the same wires on the sheet: input = rkb; output = ttwe; sw = se
endmodule

module signextend (
  input  [5:0] \input ,
  output [15:0] out
);


  assign out = {{11{\input [5]}}, \input [4:0]};
endmodule
